# Fritzing sketch BIOM 300 (saved by Fritzing 0.9.4)
breadboards: 1

parts:
  U1 = NodeMCU V3.0
  J1 = Piezo Speaker
  J2 = Basic Force Sensing Resistor (FSR) [package=THT]
  R1 = Resistor [tolerance=±5% resistance=220 package="2010 [SMD]"]

nets:
  N1: U1.D1, J1.pin2
  N2: U1.3V3, J2.pin_1
  N3: U1.GND#6, U1.GND#13, U1.GND#16, U1.GND#33, J1.pin1, R1.Pin_0
  N4: U1.A0, J2.pin_0, R1.Pin_1

custom parts:
  NodeMCU V3.0: ESP8266 based NodeMCU
